// Logisim project lab5.circ as structural Verilog: 8 circuits, main circuit main
module main (
  output [7:0] out_1,
  output [7:0] out_2
);

  AddMachine addmachine_1 (.Output(out_1), .intermediate(out_2));
endmodule

module NAND (
  input  input_1,
  input  input_2,
  output \output 
);

  wire and_1_out;

  and and_1 (and_1_out, input_1, input_2);
  not not_1 (\output , and_1_out);
endmodule

module NOR (
  input  in_1,
  input  in_2,
  output out_3
);

  wire or_1_out;

  or or_1 (or_1_out, in_1, in_2);
  not not_1 (out_3, or_1_out);
endmodule

module XOR (
  input  in_1,
  input  in_2,
  output out_3
);

  wire and_1_out, not_1_out, or_1_out;

  or or_1 (or_1_out, in_1, in_2);
  and and_1 (and_1_out, in_1, in_2);
  not not_1 (not_1_out, and_1_out);
  and and_2 (out_3, or_1_out, not_1_out);
endmodule

module _2_to_1_MUX (
  input  a,
  input  x,
  input  b,
  output out_4
);

  wire and_1_out, and_2_out, not_1_out;

  not not_1 (not_1_out, x);
  and and_1 (and_1_out, a, not_1_out);
  and and_2 (and_2_out, x, b);
  or or_1 (out_4, and_1_out, and_2_out);
endmodule

module _4_to_1_MUX (
  input  in_1,
  input  in_2,
  input  in_3,
  input  in_4,
  input  in_5,
  input  in_6,
  output out_7
);

  wire and_1_out, and_2_out, and_3_out, and_4_out, not_1_out, not_2_out;

  not not_1 (not_1_out, in_1);
  not not_2 (not_2_out, in_2);
  and and_1 (and_1_out, not_2_out, in_3, not_1_out);
  and and_2 (and_2_out, not_1_out, in_4, in_2);
  and and_3 (and_3_out, in_1, in_5, not_2_out);
  and and_4 (and_4_out, in_1, in_6, in_2);
  or or_1 (out_7, and_1_out, and_2_out, and_3_out, and_4_out);
endmodule

module XNOR (
  input  [1:0] in_1,
  input  [1:0] in_2,
  output [1:0] out_3
);

  wire [1:0] and_1_out, and_2_out, not_1_out, not_2_out;

  assign not_1_out = ~in_1;  // NOT_Gate not_1, 2 bits wide
  assign not_2_out = ~in_2;  // NOT_Gate not_2, 2 bits wide
  assign and_1_out = in_1 & in_2;  // AND_Gate and_1, 2 bits wide
  assign and_2_out = not_1_out & not_2_out;  // AND_Gate and_2, 2 bits wide
  assign out_3 = and_1_out | and_2_out;  // OR_Gate or_1, 2 bits wide
endmodule

module AddMachine (
  output [7:0] Output,
  output [7:0] intermediate
);

  wire clock_1_out;

  Clock clock_1 (.out(clock_1_out));
  Adder adder_1 (.a(intermediate), .b(8'h1), .out(Output));  // open: cin, cout
  Register register_1 (.D(Output), .Q(intermediate), .clk(clock_1_out));  // open: en, clr
endmodule
