// Logisim project lab6ALU.circ as structural Verilog: 7 circuits, main circuit ALU
// LAB12-ALU
module ALU (
  input  [31:0] ALU_Source_1,
  input  [31:0] ALU_Source_2,
  input  [2:0] ALU_Control,
  output [31:0] ALU_Result
);

  wire [4:0] bit_extender_1_out;
  wire [31:0] _000, _001, _010, _011, _100, _101, _110, _111;

  // Probe on ALU_Source_1
  // Probe on ALU_Source_2
  Bit_Extender #(.in_width(32), .out_width(5)) bit_extender_1 (.in(ALU_Source_2), .out(bit_extender_1_out));
  Shifter #(.width(32)) shifter_1 (.in(ALU_Source_1), .\dist (bit_extender_1_out), .out(_000));
  Shifter #(.width(32), .shift("lr")) shifter_2 (.in(ALU_Source_1), .\dist (bit_extender_1_out), .out(_001));
  Shifter #(.width(32), .shift("ar")) shifter_3 (.in(ALU_Source_1), .\dist (bit_extender_1_out), .out(_010));
  Shifter #(.width(32), .shift("rl")) shifter_4 (.in(ALU_Source_1), .\dist (bit_extender_1_out), .out(_011));
  Shifter #(.width(32), .shift("rr")) shifter_5 (.in(ALU_Source_1), .\dist (bit_extender_1_out), .out(_100));
  assign _101 = ALU_Source_1 & ALU_Source_2;  // AND_Gate and_1, 32 bits wide
  assign _110 = ALU_Source_1 | ALU_Source_2;  // OR_Gate or_1, 32 bits wide
  assign _111 = ALU_Source_1 ^ ALU_Source_2;  // XOR_Gate xor_1, 32 bits wide
  // Probe on ALU_Result
  Multiplexer #(.select(3), .width(32), .enable("false")) multiplexer_1 (
    .in0(_000), .in1(_001), .in2(_010), .in3(_011), .in4(_100), .in5(_101), .in6(_110), .in7(_111),
    .out(ALU_Result), .sel(ALU_Control));

  // Other names for the same wires on the sheet: control[2:0] = ALU_Control; result[31:0] = ALU_Result;
  //   source1[31:0] = ALU_Source_1; source2[31:0] = ALU_Source_2

  // Notes on the sheet:
  //   DO NOT CROSS WIRES
  //   OVER THIS BOX
  //   DO NOT CROSS WIRES
  //   OVER THIS BOX
  //   COMPUTE ALL POSSIBLE OPERATIONS
  //   DO NOT CROSS WIRES
  //   OVER THIS BOX
  //   DO NOT CROSS WIRES
  //   OVER THIS BOX
  //   SELECT THE REQUESTED RESULT
endmodule

module Ex1 (
  input  [7:0] \input ,
  output Out1,
  output [7:0] Out2
);

  not not_1 (Out2[7], \input [7]);
  and and_1 (Out1, \input [0], \input [7]);

  assign Out2[6:0] = \input [6:0];
endmodule

module rotr (
  input  [15:0] Input_number,
  input  [3:0] Shift_amount,
  output [15:0] out_3
);

  wire [15:0] multiplexer_1_out, multiplexer_2_out, multiplexer_3_out, n1shift_1_out_2, n2shift_1_out_2,
       n4shift_1_out_2, n8shift_1_out_2;

  _1shift u_1shift_1 (.Source_1(Input_number), .out_2(n1shift_1_out_2));
  Multiplexer #(.width(16), .enable("false")) multiplexer_1 (
    .in0(Input_number), .in1(n1shift_1_out_2), .out(multiplexer_1_out), .sel(Shift_amount[0]));
  _2shift u_2shift_1 (.Source_1(multiplexer_1_out), .out_2(n2shift_1_out_2));
  Multiplexer #(.width(16), .enable("false")) multiplexer_2 (
    .in0(multiplexer_1_out), .in1(n2shift_1_out_2), .out(multiplexer_2_out), .sel(Shift_amount[1]));
  _4shift u_4shift_1 (.Source_1(multiplexer_2_out), .out_2(n4shift_1_out_2));
  Multiplexer #(.width(16), .enable("false")) multiplexer_3 (
    .in0(multiplexer_2_out), .in1(n4shift_1_out_2), .out(multiplexer_3_out), .sel(Shift_amount[2]));
  _8shift u_8shift_1 (.Source_1(multiplexer_3_out), .out_2(n8shift_1_out_2));
  Multiplexer #(.width(16), .enable("false")) multiplexer_4 (
    .in0(multiplexer_3_out), .in1(n8shift_1_out_2), .out(out_3), .sel(Shift_amount[3]));
endmodule

module _1shift (
  input  [15:0] Source_1,
  output [15:0] out_2
);


  assign out_2 = {Source_1[0], Source_1[15:1]};
endmodule

module _2shift (
  input  [15:0] Source_1,
  output [15:0] out_2
);


  assign out_2 = {Source_1[1:0], Source_1[15:2]};
endmodule

module _4shift (
  input  [15:0] Source_1,
  output [15:0] out_2
);


  assign out_2 = {Source_1[3:0], Source_1[15:4]};
endmodule

module _8shift (
  input  [15:0] Source_1,
  output [15:0] out_2
);


  assign out_2 = {Source_1[7:0], Source_1[15:8]};
endmodule
