// Logisim project pipeline.circ as structural Verilog: 3 circuits, main circuit main
module main (
  output [7:0] Non_pipelined_Out,
  output [7:0] Pipelined_Out
);

  wire CLK_out;
  wire [7:0] Address_Counter_q, rom_1_data;

  Clock CLK (.out(CLK_out));
  Counter Address_Counter (.Q(Address_Counter_q), .clk(CLK_out));  // open: load, D, count, carry, clr
  ROM rom_1 (.addr(Address_Counter_q), .data(rom_1_data));  // open: sel
  Non_pipelined Non_pipelined (.Input1(8'h1), .Input2(rom_1_data), .CLK(CLK_out), .out_4(Non_pipelined_Out));
  Pipelined Pipelined (.In2(8'h1), .In3(rom_1_data), .CLK(CLK_out), .Pipelined_Out(Pipelined_Out));
  // Probe on Non_pipelined_Out
  // Probe on Pipelined_Out

  // Notes on the sheet:
  //   contents of rom_1 (hex, n*v repeats v):
  //   3 2 fc 1 2 fb 1
endmodule

module Non_pipelined (
  input  [7:0] Input1,
  input  [7:0] Input2,
  input  CLK,
  output [7:0] out_4
);

  wire [7:0] adder_1_out, multiplier_1_out;

  Multiplier multiplier_1 (.a(Input1), .b(Input2), .out(multiplier_1_out));  // open: cin, cout
  Adder adder_1 (.a(multiplier_1_out), .b(out_4), .out(adder_1_out), .cin(Input1[7]));  // open: cout
  Register register_1 (.D(adder_1_out), .Q(out_4), .clk(CLK));  // open: en, clr
endmodule

module Pipelined (
  input  [7:0] In2,
  input  [7:0] In3,
  input  CLK,
  output [7:0] Pipelined_Out
);

  wire [7:0] adder_1_out, clk_t, multiplier_1_out;

  Multiplier multiplier_1 (.a(In2), .b(In3), .out(multiplier_1_out));  // open: cin, cout
  Adder adder_1 (.a(Pipelined_Out), .b(clk_t), .out(adder_1_out), .cin(In2[7]));  // open: cout
  Register register_1 (.D(multiplier_1_out), .Q(clk_t), .clk(CLK));  // open: en, clr
  Register register_2 (.D(adder_1_out), .Q(Pipelined_Out), .clk(CLK));  // open: en, clr
endmodule
