// Logisim project alu.circ as structural Verilog: 1 circuit, main circuit main
module main (
  input  [31:0] X,
  input  [31:0] Y,
  input  [3:0] Switch,
  output Signed_Overflow,
  output Equal,
  output [31:0] Result,
  output [31:0] Result_2
);

  wire and_1_out, and_2_out, comparator_2_eq, comparator_3_eq, comparator_4_eq, comparator_5_eq,
       comparator_6_eq, comparator_7_eq, comparator_8_eq, comparator_9_eq, comparator_10_lt,
       comparator_11_lt, not_1_out, not_2_out, over1, over2;
  wire [1:0] bit_extender_2_out, bit_extender_3_out, bit_extender_4_out, bit_extender_5_out,
       multiplier_1_out, multiplier_2_out, or_1_out, or_2_out;
  wire [4:0] shift_amount;
  wire [31:0] adder_1_out, and_3_out, bit_extender_6_out, bit_extender_7_out, divider_1_out, h_result21,
       h_result22, multiplier_3_out, nor_1_out, or_3_out, shifter_1_out, shifter_2_out, shifter_3_out,
       subtractor_1_out, xor_1_out;

  Bit_Extender #(.in_width(32), .out_width(5)) bit_extender_1 (.in(X), .out(shift_amount));
  Comparator #(.width(32)) comparator_1 (.a(X), .b(Y), .eq(Equal));  // open: gt, lt
  Comparator #(.width(4)) comparator_2 (.a(Switch), .b(4'b0011), .eq(comparator_2_eq));  // open: gt, lt
  Comparator #(.width(4)) comparator_3 (.a(Switch), .b(4'b0100), .eq(comparator_3_eq));  // open: gt, lt
  Comparator #(.width(4)) comparator_4 (.a(Switch), .b(4'b0101), .eq(comparator_4_eq));  // open: gt, lt
  Comparator #(.width(4)) comparator_5 (.a(Switch), .b(4'b0111), .eq(comparator_5_eq));  // open: gt, lt
  assign bit_extender_2_out = {{1{1'b0}}, comparator_2_eq};  // Bit_Extender bit_extender_2
  assign bit_extender_3_out = {{1{1'b0}}, comparator_3_eq};  // Bit_Extender bit_extender_3
  Comparator #(.width(1)) comparator_6 (.a(X[31]), .b(Y[31]), .eq(comparator_6_eq));  // open: gt, lt
  not not_1 (not_1_out, comparator_7_eq);
  Comparator #(.width(1)) comparator_7 (.a(X[31]), .b(Result[31]), .eq(comparator_7_eq));  // open: gt, lt
  Comparator #(.width(1)) comparator_8 (.a(X[31]), .b(Y[31]), .eq(comparator_8_eq));  // open: gt, lt
  not not_2 (not_2_out, comparator_8_eq);
  Comparator #(.width(1)) comparator_9 (.a(Y[31]), .b(Result[31]), .eq(comparator_9_eq));  // open: gt, lt
  assign bit_extender_4_out = {{1{1'b0}}, comparator_4_eq};  // Bit_Extender bit_extender_4
  assign bit_extender_5_out = {{1{1'b0}}, comparator_5_eq};  // Bit_Extender bit_extender_5
  assign or_1_out = bit_extender_2_out | multiplier_1_out;  // OR_Gate or_1, 2 bits wide
  Multiplier #(.width(2)) multiplier_1 (.a(bit_extender_3_out), .b(2'b10), .out(multiplier_1_out));  // open: cin, cout
  and and_1 (and_1_out, comparator_6_eq, not_1_out);
  Multiplexer #(.enable("false")) multiplexer_1 (.in0(1'b0), .in1(1'b1), .out(over1), .sel(and_1_out));
  and and_2 (and_2_out, not_2_out, comparator_9_eq);
  Multiplexer #(.enable("false")) multiplexer_2 (.in0(1'b0), .in1(1'b1), .out(over2), .sel(and_2_out));
  assign or_2_out = bit_extender_4_out | multiplier_2_out;  // OR_Gate or_2, 2 bits wide
  Multiplier #(.width(2)) multiplier_2 (.a(bit_extender_5_out), .b(2'b10), .out(multiplier_2_out));  // open: cin, cout
  Multiplexer #(.select(2), .width(32), .enable("false")) multiplexer_3 (
    .in0({32{1'b0}}), .in1(h_result21), .in2(h_result22), .in3({32{1'b0}}), .out(Result_2), .sel(or_1_out));
  Multiplexer #(.select(2), .enable("false")) multiplexer_4 (
    .in0(1'b0), .in1(over1), .in2(over2), .in3(1'b0), .out(Signed_Overflow), .sel(or_2_out));
  Comparator #(.width(32)) comparator_10 (.a(X), .b(Y), .lt(comparator_10_lt));  // open: gt, eq
  Comparator #(.width(32), .mode("unsigned")) comparator_11 (.a(X), .b(Y), .lt(comparator_11_lt));  // open: gt, eq
  Shifter #(.width(32)) shifter_1 (.in(Y), .\dist (shift_amount), .out(shifter_1_out));
  Shifter #(.width(32), .shift("lr")) shifter_2 (.in(Y), .\dist (shift_amount), .out(shifter_2_out));
  Shifter #(.width(32), .shift("ar")) shifter_3 (.in(Y), .\dist (shift_amount), .out(shifter_3_out));
  Multiplier #(.width(32)) multiplier_3 (.a(X), .b(Y), .out(multiplier_3_out), .cout(h_result21));  // open: cin
  Divider #(.width(32)) divider_1 (.a(X), .b(Y), .out(divider_1_out), .rem(h_result22));  // open: upper
  Adder #(.width(32)) adder_1 (.a(X), .b(Y), .out(adder_1_out));  // open: cin, cout
  Subtractor #(.width(32)) subtractor_1 (.a(X), .b(Y), .out(subtractor_1_out));  // open: bin, bout
  assign and_3_out = X & Y;  // AND_Gate and_3, 32 bits wide
  assign or_3_out = X | Y;  // OR_Gate or_3, 32 bits wide
  assign xor_1_out = X ^ Y;  // XOR_Gate xor_1, 32 bits wide
  assign nor_1_out = ~(X | Y);  // NOR_Gate nor_1, 32 bits wide
  assign bit_extender_6_out = {{31{1'b0}}, comparator_10_lt};  // Bit_Extender bit_extender_6
  assign bit_extender_7_out = {{31{1'b0}}, comparator_11_lt};  // Bit_Extender bit_extender_7
  Multiplexer #(.select(4), .width(32), .enable("false")) multiplexer_5 (
    .in0(shifter_1_out), .in1(shifter_2_out), .in2(shifter_3_out), .in3(multiplier_3_out),
    .in4(divider_1_out), .in5(adder_1_out), .in6(adder_1_out), .in7(subtractor_1_out),
    .in8(subtractor_1_out), .in9(and_3_out), .in10(or_3_out), .in11(xor_1_out), .in12(nor_1_out),
    .in13(bit_extender_6_out), .in14(bit_extender_7_out), .in15({32{1'b0}}), .out(Result), .sel(Switch));

  // Other names for the same wires on the sheet: overflow = Signed_Overflow; S[3:0] = Switch

  // Notes on the sheet:
  //   INPUTS to your circuit
  //   DON'T CHANGE THE LOCATIONS OF THE INPUTS AND OUTPUTS!
  //   OUTPUTS from your circuit
endmodule
