// Logisim project cpu-test.circ as structural Verilog: 3 circuits, main circuit main
module main (
  input  [31:0] INSTRUCTION,
  input  CLOCK,
  output [31:0] FETCH_ADDRESS,
  output [31:0] s0_Value,
  output [31:0] s1_Value,
  output [31:0] s2_Value,
  output [31:0] ra_Value,
  output [31:0] sp_Value,
  output [31:0] HI_Value,
  output [31:0] LO_Value
);

  wire cBranch, cCRA, cImm, cIsBEQINC, cIsLUI, cIsMFHI, cIsMFLO, cIsMultDiv, cJal_r, cJump, cLW, cMemWrite,
       cRegDst, cRegWrite, cShift, cSXT, main_2_signed_overflow, or_1_out, register_1_q, Zero;
  wire [3:0] cALU;
  wire [4:0] multiplexer_3_out, multiplexer_5_out, rd, rs, rt, split_instruct_1_shamt;
  wire [5:0] split_instruct_1_funct, split_instruct_1_opcode;
  wire [15:0] imm_b;
  wire [31:0] adder_1_out, adder_2_out, adder_3_out, beqinc1, bit_extender_2_out, bit_extender_3_out, high,
       imm, INSTRUCTION_Next, JAddr, JAddr1, jal_r, low, MEM_p5, multiplexer_1_out, multiplexer_2_out,
       multiplexer_4_out, multiplexer_6_out, multiplexer_8_out, multiplexer_9_out, multiplexer_10_out,
       multiplexer_11_out, multiplexer_13_out, multiplexer_14_out, multiplexer_16_out, multiplexer_17_out,
       Pipelining_q, shamt, shifter_1_out, shifter_2_out;

  Adder #(.width(32)) adder_1 (.a(FETCH_ADDRESS), .b(32'h4), .out(adder_1_out));  // open: cin, cout
  Shifter #(.width(32)) shifter_1 (.in(imm), .\dist (5'b00010), .out(shifter_1_out));
  split_instruct split_instruct_1 (
    .instruction(INSTRUCTION_Next), .PC(FETCH_ADDRESS), .shamt(split_instruct_1_shamt), .rd(rd), .rt(rt),
    .rs(rs), .funct(split_instruct_1_funct), .opcode(split_instruct_1_opcode), .Imm(imm_b), .JAddr(JAddr1));
  Adder #(.width(32)) adder_2 (.a(FETCH_ADDRESS), .b(shifter_1_out), .out(adder_2_out));  // open: cin, cout
  assign shamt = {{27{split_instruct_1_shamt[4]}}, split_instruct_1_shamt};  // Bit_Extender bit_extender_1
  controller controller_1 (
    .Func(split_instruct_1_funct), .OpCode(split_instruct_1_opcode), .Zero(Zero), .cALU(cALU),
    .cBranch(cBranch), .cJump(cJump), .cRegDst(cRegDst), .cRegWrite(cRegWrite), .cImm(cImm), .cLW(cLW),
    .cMemWrite(cMemWrite), .cShift(cShift), .cFix_RA(cCRA), .cIsMultDiv(cIsMultDiv), .cIsMFLO(cIsMFLO),
    .cIsMFHI(cIsMFHI), .cIsLUI(cIsLUI), .cIsBEQINC(cIsBEQINC), .cSXT(cSXT), .cJal_r(cJal_r));
  Multiplexer #(.width(32), .enable("false")) multiplexer_1 (
    .in0(multiplexer_2_out), .in1(JAddr), .out(multiplexer_1_out), .sel(cJump));
  Multiplexer #(.width(32), .enable("false")) multiplexer_2 (
    .in0(adder_1_out), .in1(adder_2_out), .out(multiplexer_2_out), .sel(cBranch));
  Register #(.width(32)) PC (.D(multiplexer_1_out), .Q(FETCH_ADDRESS), .clk(CLOCK));  // open: en, clr
  Multiplexer #(.width(5), .enable("false")) multiplexer_3 (.in0(rd), .in1(rt), .out(multiplexer_3_out), .sel(cRegDst));
  Multiplexer #(.width(32), .enable("false")) multiplexer_4 (
    .in0(multiplexer_6_out), .in1(adder_3_out), .out(multiplexer_4_out), .sel(cIsBEQINC));
  Register #(.width(32)) Pipelining (.D(INSTRUCTION), .Q(Pipelining_q), .clk(CLOCK));  // open: en, clr
  Multiplexer #(.width(5), .enable("false")) multiplexer_5 (
    .in0(multiplexer_3_out), .in1({5{1'b1}}), .out(multiplexer_5_out), .sel(cCRA));
  Adder #(.width(32)) adder_3 (.a(beqinc1), .b(32'h1), .out(adder_3_out));  // open: cin, cout
  or or_1 (or_1_out, cBranch, cJump);
  Multiplexer #(.width(32), .enable("false")) multiplexer_6 (
    .in0(multiplexer_8_out), .in1(shifter_2_out), .out(multiplexer_6_out), .sel(cIsLUI));
  Shifter #(.width(32)) shifter_2 (.in(imm), .\dist (5'b10000), .out(shifter_2_out));
  Register #(.width(1)) register_1 (.D(or_1_out), .Q(register_1_q), .clk(CLOCK));  // open: en, clr
  Multiplexer #(.width(32), .enable("false")) multiplexer_7 (
    .in0(Pipelining_q), .in1({32{1'b0}}), .out(INSTRUCTION_Next), .sel(register_1_q));
  regfile_main main_1 (
    .Read_Register_1(rs), .Read_Register_2(rt), .Write_Register(multiplexer_5_out),
    .Write_Data(multiplexer_4_out), .Write_Enable(cRegWrite), .Clock(CLOCK), .Read_Data_1(jal_r),
    .Read_Data_2(beqinc1), .s0_Value(s0_Value), .s1_Value(s1_Value), .s2_Value(s2_Value),
    .ra_Value(ra_Value), .sp_Value(sp_Value));
  Multiplexer #(.width(32), .enable("false")) multiplexer_8 (
    .in0(multiplexer_9_out), .in1(HI_Value), .out(multiplexer_8_out), .sel(cIsMFHI));
  Multiplexer #(.width(32), .enable("false")) multiplexer_9 (
    .in0(multiplexer_11_out), .in1(LO_Value), .out(multiplexer_9_out), .sel(cIsMFLO));
  Multiplexer #(.width(32), .enable("false")) multiplexer_10 (
    .in0(beqinc1), .in1(imm), .out(multiplexer_10_out), .sel(cImm));
  Multiplexer #(.width(32), .enable("false")) multiplexer_11 (
    .in0(multiplexer_14_out), .in1(FETCH_ADDRESS), .out(multiplexer_11_out), .sel(cCRA));
  Multiplexer #(.width(32), .enable("false")) multiplexer_12 (.in0(JAddr1), .in1(jal_r), .out(JAddr), .sel(cJal_r));
  assign bit_extender_2_out = {{16{1'b0}}, imm_b};  // Bit_Extender bit_extender_2
  assign bit_extender_3_out = {{16{imm_b[15]}}, imm_b};  // Bit_Extender bit_extender_3
  LED Overflow (.in(main_2_signed_overflow));
  Multiplexer #(.width(32), .enable("false")) multiplexer_13 (
    .in0(jal_r), .in1(shamt), .out(multiplexer_13_out), .sel(cShift));
  alu_main main_2 (
    .Switch(cALU), .X(multiplexer_13_out), .Equal(Zero), .Result(low),
    .Signed_Overflow(main_2_signed_overflow), .Y(multiplexer_10_out), .Result_2(high));
  Multiplexer #(.width(32), .enable("false")) multiplexer_14 (
    .in0(low), .in1(MEM_p5), .out(multiplexer_14_out), .sel(cLW));
  Multiplexer #(.width(32), .enable("false")) multiplexer_15 (
    .in0(bit_extender_2_out), .in1(bit_extender_3_out), .out(imm), .sel(cSXT));
  Multiplexer #(.width(32), .enable("false")) multiplexer_16 (
    .in0(LO_Value), .in1(low), .out(multiplexer_16_out), .sel(cIsMultDiv));
  Register #(.width(32)) LO (.D(multiplexer_16_out), .Q(LO_Value), .clk(CLOCK));  // open: en, clr
  Register #(.width(32)) HI (.D(multiplexer_17_out), .Q(HI_Value), .clk(CLOCK));  // open: en, clr
  Multiplexer #(.width(32), .enable("false")) multiplexer_17 (
    .in0(HI_Value), .in1(high), .out(multiplexer_17_out), .sel(cIsMultDiv));
  // mem_main MEM: pin names not known; wires that end beside it: low, beqinc1, cMemWrite, CLOCK, MEM_p5

  // Other names for the same wires on the sheet: clk = CLOCK; HI[31:0] = HI_Value; mfhi[31:0] = HI_Value;
  //   LO[31:0] = LO_Value; mflo[31:0] = LO_Value; fetch_addr[31:0] = FETCH_ADDRESS; PC_4[31:0] = FETCH_ADDRESS;
  //   pc_cur[31:0] = FETCH_ADDRESS; ra[31:0] = ra_Value; s0[31:0] = s0_Value; s1[31:0] = s1_Value;
  //   s2[31:0] = s2_Value; sp[31:0] = sp_Value

  // Notes on the sheet:
  //   Output
  //   These are outputs/inputs from run.circ
  //   Inputs
  //   These are DEBUG/TEST outputs from your circuit.
endmodule

// split
module split_instruct (
  input  [31:0] instruction,
  input  [31:0] PC,
  output [4:0] shamt,
  output [4:0] rd,
  output [4:0] rt,
  output [4:0] rs,
  output [5:0] funct,
  output [5:0] opcode,
  output [15:0] Imm,
  output [31:0] JAddr
);


  assign funct = instruction[5:0];
  assign Imm = instruction[15:0];
  assign JAddr = {PC[31:28], instruction[25:0], 2'b00};
  assign opcode = instruction[31:26];
  assign rd = instruction[15:11];
  assign rs = instruction[25:21];
  assign rt = instruction[20:16];
  assign shamt = instruction[10:6];

  // Notes on the sheet:
  //   funct: pull=down
endmodule

// Controller
module controller (
  input  [5:0] Func,
  input  [5:0] OpCode,
  input  Zero,
  output [3:0] cALU,
  output cBranch,
  output cJump,
  output cRegDst,
  output cRegWrite,
  output cImm,
  output cLW,
  output cMemWrite,
  output cShift,
  output cFix_RA,
  output cIsMultDiv,
  output cIsMFLO,
  output cIsMFHI,
  output cIsLUI,
  output cIsBEQINC,
  output cSXT,
  output cJal_r
);

  wire add, addi, addiu, addu, \and , and_1_out, and_2_out, and_3_out, and_4_out, and_6_out, and_7_out,
       and_8_out, and_9_out, and_12_out, andi, beq, beqinc, bne, divu, j, jal, jalr, jr, mfhi, mflo, mult,
       \nor , not_1_out, not_2_out, not_3_out, not_4_out, not_5_out, not_6_out, not_7_out, not_8_out,
       not_9_out, not_10_out, not_11_out, not_12_out, not_13_out, not_14_out, not_15_out, not_16_out,
       not_17_out, not_18_out, not_19_out, not_20_out, not_21_out, not_22_out, not_23_out, not_24_out,
       not_25_out, not_26_out, not_27_out, not_28_out, not_29_out, not_30_out, not_31_out, not_32_out,
       not_33_out, not_34_out, not_35_out, not_36_out, not_37_out, not_38_out, not_39_out, not_40_out,
       not_41_out, not_42_out, not_43_out, not_44_out, not_45_out, not_46_out, not_47_out, not_48_out,
       not_49_out, not_50_out, not_51_out, not_52_out, not_53_out, not_54_out, not_55_out, not_56_out,
       not_57_out, not_58_out, not_59_out, not_60_out, not_61_out, not_62_out, not_63_out, not_64_out,
       not_65_out, not_66_out, not_67_out, not_68_out, not_69_out, not_70_out, not_71_out, not_72_out,
       not_73_out, not_74_out, not_75_out, not_76_out, not_77_out, not_78_out, not_79_out, not_80_out,
       not_81_out, not_82_out, not_83_out, not_84_out, not_85_out, not_86_out, not_87_out, not_88_out,
       not_89_out, not_90_out, not_91_out, not_92_out, not_93_out, not_94_out, not_95_out, not_96_out,
       not_97_out, not_98_out, not_99_out, not_100_out, not_101_out, not_102_out, not_103_out, not_104_out,
       not_105_out, not_106_out, not_107_out, not_108_out, not_109_out, not_110_out, not_111_out,
       not_112_out, not_113_out, not_114_out, not_115_out, not_116_out, not_117_out, not_118_out,
       not_119_out, not_120_out, not_121_out, not_122_out, not_123_out, not_124_out, not_125_out,
       not_126_out, not_127_out, not_128_out, not_129_out, not_130_out, not_131_out, not_132_out, OpZero,
       \or , or_1_out, or_2_out, or_3_out, or_7_out, or_8_out, or_13_out, or_15_out, or_17_out, ori, sll,
       slt, slti, sltiu, sltu, sra, srl, sub, subu, \xor , xori;
  wire [3:0] bit_extender_1_out, bit_extender_2_out, bit_extender_3_out, bit_extender_4_out,
       bit_extender_5_out, bit_extender_6_out, bit_extender_7_out, bit_extender_8_out, bit_extender_9_out,
       bit_extender_10_out, bit_extender_11_out, bit_extender_12_out, bit_extender_13_out,
       bit_extender_14_out, bit_extender_15_out, bit_extender_16_out, bit_extender_17_out,
       bit_extender_18_out, bit_extender_19_out, bit_extender_20_out, bit_extender_21_out,
       bit_extender_22_out, bit_extender_23_out, bit_extender_24_out, bit_extender_25_out,
       bit_extender_26_out, bit_extender_27_out, bit_extender_28_out, bit_extender_29_out,
       bit_extender_30_out, bit_extender_31_out, bit_extender_32_out, bit_extender_33_out,
       bit_extender_34_out, cALU_JI, cALU_R, multiplier_1_out, multiplier_2_out, multiplier_3_out,
       multiplier_4_out, multiplier_5_out, multiplier_6_out, multiplier_7_out, multiplier_8_out,
       multiplier_9_out, multiplier_10_out, multiplier_11_out, multiplier_12_out, multiplier_13_out,
       multiplier_14_out, multiplier_15_out, multiplier_16_out, multiplier_17_out, multiplier_18_out,
       multiplier_19_out, multiplier_20_out, multiplier_21_out, multiplier_22_out, multiplier_23_out,
       multiplier_24_out, multiplier_25_out, multiplier_26_out, multiplier_27_out, multiplier_28_out,
       multiplier_29_out, multiplier_30_out, multiplier_31_out, multiplier_32_out;

  Comparator #(.width(6), .mode("unsigned")) comparator_1 (.a(OpCode), .b({6{1'b0}}), .eq(OpZero));  // open: gt, lt
  and and_1 (and_1_out, Zero, beq);
  and and_2 (and_2_out, ~Zero, bne);  // AND_Gate
  and and_3 (and_3_out, Zero, beqinc);
  or or_1 (or_1_out, j, jal);
  or or_2 (or_2_out, jalr, jr);
  and and_4 (and_4_out, or_2_out, OpZero);
  or or_3 (or_3_out, cRegDst, cMemWrite);
  not not_1 (not_1_out, beqinc);
  or or_4 (cBranch, and_1_out, and_2_out, and_3_out);
  or or_5 (cJump, or_1_out, and_4_out);
  or or_6 (cRegDst, beqinc, addi, addiu, slti, sltiu, andi, ori, xori, cIsLUI, cLW);
  and and_5 (cImm, or_3_out, not_1_out);
  or or_7 (or_7_out, sll, srl, sra, jalr, mfhi, mflo, add, addu, subu, \and , \nor , \or , \xor , slt, sltu, sub);
  and and_6 (and_6_out, beqinc, not_2_out);
  not not_2 (not_2_out, Zero);
  and and_7 (and_7_out, cRegDst, not_3_out);
  not not_3 (not_3_out, beqinc);
  and and_8 (and_8_out, or_7_out, OpZero);
  or or_8 (or_8_out, and_6_out, and_7_out);
  or or_9 (cRegWrite, and_8_out, or_8_out, jal);
  not not_4 (not_4_out, Func[0]);
  not not_5 (not_5_out, Func[5]);
  not not_6 (not_6_out, Func[4]);
  not not_7 (not_7_out, Func[3]);
  not not_8 (not_8_out, Func[2]);
  not not_9 (not_9_out, Func[1]);
  and u_sll (sll, not_5_out, not_6_out, not_7_out, not_8_out, not_9_out, not_4_out);
  and and_9 (and_9_out, 1'b0, sll);
  assign bit_extender_1_out = {{3{1'b0}}, and_9_out};  // Bit_Extender bit_extender_1
  not not_10 (not_10_out, OpCode[3]);
  not not_11 (not_11_out, OpCode[5]);
  not not_12 (not_12_out, OpCode[4]);
  not not_13 (not_13_out, OpCode[2]);
  and u_j (j, not_11_out, not_12_out, not_10_out, not_13_out, OpCode[1], not_21_out);
  not not_14 (not_14_out, Func[2]);
  not not_15 (not_15_out, Func[3]);
  not not_16 (not_16_out, Func[4]);
  not not_17 (not_17_out, Func[5]);
  not not_18 (not_18_out, Func[0]);
  and u_srl (srl, not_17_out, not_16_out, not_15_out, not_14_out, Func[1], not_18_out);
  not not_19 (not_19_out, OpCode[3]);
  not not_20 (not_20_out, OpCode[4]);
  not not_21 (not_21_out, OpCode[0]);
  not not_22 (not_22_out, OpCode[5]);
  and u_jal (jal, not_22_out, not_20_out, not_19_out, not_28_out, OpCode[1], OpCode[0]);
  assign bit_extender_2_out = {{3{1'b0}}, j};  // Bit_Extender bit_extender_2
  Multiplier #(.width(4)) multiplier_1 (
    .a(bit_extender_2_out), .b(4'b1111), .out(multiplier_1_out));  // open: cin, cout
  not not_23 (not_23_out, Func[5]);
  not not_24 (not_24_out, Func[3]);
  not not_25 (not_25_out, Func[2]);
  not not_26 (not_26_out, Func[4]);
  and u_sra (sra, not_23_out, not_26_out, not_24_out, not_25_out, Func[1], Func[0]);
  assign bit_extender_3_out = {{3{1'b0}}, srl};  // Bit_Extender bit_extender_3
  not not_27 (not_27_out, OpCode[5]);
  not not_28 (not_28_out, OpCode[2]);
  not not_29 (not_29_out, OpCode[4]);
  not not_30 (not_30_out, OpCode[3]);
  assign bit_extender_4_out = {{3{1'b0}}, jal};  // Bit_Extender bit_extender_4
  Multiplier #(.width(4)) multiplier_2 (
    .a(bit_extender_4_out), .b(4'b1111), .out(multiplier_2_out));  // open: cin, cout
  not not_31 (not_31_out, Func[2]);
  not not_32 (not_32_out, Func[5]);
  not not_33 (not_33_out, Func[0]);
  not not_34 (not_34_out, Func[1]);
  not not_35 (not_35_out, Func[4]);
  and u_jr (jr, not_32_out, not_35_out, Func[3], not_31_out, not_34_out, not_33_out);
  assign bit_extender_5_out = {{3{1'b0}}, sra};  // Bit_Extender bit_extender_5
  Multiplier #(.width(4)) multiplier_3 (
    .a(bit_extender_5_out), .b(4'b0010), .out(multiplier_3_out));  // open: cin, cout
  not not_36 (not_36_out, OpCode[1]);
  not not_37 (not_37_out, OpCode[0]);
  not not_38 (not_38_out, OpCode[5]);
  not not_39 (not_39_out, OpCode[4]);
  and u_beq (beq, not_27_out, not_29_out, not_30_out, OpCode[2], not_36_out, not_37_out);
  assign bit_extender_6_out = {{3{1'b0}}, beq};  // Bit_Extender bit_extender_6
  Multiplier #(.width(4)) multiplier_4 (
    .a(bit_extender_6_out), .b(4'b1111), .out(multiplier_4_out));  // open: cin, cout
  not not_40 (not_40_out, Func[2]);
  not not_41 (not_41_out, Func[5]);
  not not_42 (not_42_out, Func[1]);
  not not_43 (not_43_out, Func[4]);
  and u_jalr (jalr, not_41_out, not_43_out, Func[3], not_40_out, not_42_out, Func[0]);
  assign bit_extender_7_out = {{3{1'b0}}, jr};  // Bit_Extender bit_extender_7
  Multiplier #(.width(4)) multiplier_5 (
    .a(bit_extender_7_out), .b(4'b1111), .out(multiplier_5_out));  // open: cin, cout
  not not_44 (not_44_out, OpCode[3]);
  not not_45 (not_45_out, OpCode[1]);
  not not_46 (not_46_out, OpCode[5]);
  and u_bne (bne, not_38_out, not_39_out, not_44_out, OpCode[2], not_45_out, OpCode[0]);
  assign bit_extender_8_out = {{3{1'b0}}, bne};  // Bit_Extender bit_extender_8
  Multiplier #(.width(4)) multiplier_6 (
    .a(bit_extender_8_out), .b(4'b1111), .out(multiplier_6_out));  // open: cin, cout
  not not_47 (not_47_out, Func[3]);
  not not_48 (not_48_out, Func[2]);
  not not_49 (not_49_out, Func[1]);
  not not_50 (not_50_out, Func[0]);
  not not_51 (not_51_out, Func[5]);
  and u_mfhi (mfhi, not_51_out, Func[4], not_47_out, not_48_out, not_49_out, not_50_out);
  assign bit_extender_9_out = {{3{1'b0}}, jalr};  // Bit_Extender bit_extender_9
  Multiplier #(.width(4)) multiplier_7 (
    .a(bit_extender_9_out), .b(4'b1111), .out(multiplier_7_out));  // open: cin, cout
  not not_52 (not_52_out, OpCode[0]);
  not not_53 (not_53_out, OpCode[4]);
  not not_54 (not_54_out, OpCode[1]);
  not not_55 (not_55_out, OpCode[2]);
  and u_addi (addi, not_46_out, not_53_out, OpCode[3], not_55_out, not_54_out, not_52_out);
  assign bit_extender_10_out = {{3{1'b0}}, addi};  // Bit_Extender bit_extender_10
  Multiplier #(.width(4)) multiplier_8 (
    .a(bit_extender_10_out), .b(4'b0101), .out(multiplier_8_out));  // open: cin, cout
  not not_56 (not_56_out, Func[2]);
  not not_57 (not_57_out, Func[0]);
  not not_58 (not_58_out, Func[5]);
  not not_59 (not_59_out, Func[3]);
  and u_mflo (mflo, not_58_out, Func[4], not_59_out, not_56_out, Func[1], not_57_out);
  assign bit_extender_11_out = {{3{1'b0}}, mfhi};  // Bit_Extender bit_extender_11
  Multiplier #(.width(4)) multiplier_9 (
    .a(bit_extender_11_out), .b(4'b1111), .out(multiplier_9_out));  // open: cin, cout
  not not_60 (not_60_out, OpCode[2]);
  not not_61 (not_61_out, OpCode[4]);
  not not_62 (not_62_out, OpCode[1]);
  not not_63 (not_63_out, OpCode[5]);
  and u_addiu (addiu, not_63_out, not_61_out, OpCode[3], not_60_out, not_62_out, OpCode[0]);
  assign bit_extender_12_out = {{3{1'b0}}, addiu};  // Bit_Extender bit_extender_12
  Multiplier #(.width(4)) multiplier_10 (
    .a(bit_extender_12_out), .b(4'b0110), .out(multiplier_10_out));  // open: cin, cout
  not not_64 (not_64_out, Func[1]);
  not not_65 (not_65_out, Func[2]);
  not not_66 (not_66_out, Func[5]);
  not not_67 (not_67_out, Func[0]);
  and u_mult (mult, not_66_out, Func[4], Func[3], not_65_out, not_64_out, not_67_out);
  assign bit_extender_13_out = {{3{1'b0}}, mflo};  // Bit_Extender bit_extender_13
  Multiplier #(.width(4)) multiplier_11 (
    .a(bit_extender_13_out), .b(4'b1111), .out(multiplier_11_out));  // open: cin, cout
  not not_68 (not_68_out, OpCode[5]);
  not not_69 (not_69_out, OpCode[0]);
  not not_70 (not_70_out, OpCode[2]);
  not not_71 (not_71_out, OpCode[4]);
  and u_slti (slti, not_68_out, not_71_out, OpCode[3], not_70_out, OpCode[1], not_69_out);
  not not_72 (not_72_out, Func[2]);
  not not_73 (not_73_out, Func[5]);
  and u_divu (divu, not_73_out, Func[4], Func[3], not_72_out, Func[1], Func[0]);
  assign bit_extender_14_out = {{3{1'b0}}, mult};  // Bit_Extender bit_extender_14
  Multiplier #(.width(4)) multiplier_12 (
    .a(bit_extender_14_out), .b(4'b0011), .out(multiplier_12_out));  // open: cin, cout
  not not_74 (not_74_out, OpCode[5]);
  not not_75 (not_75_out, OpCode[4]);
  not not_76 (not_76_out, OpCode[2]);
  and u_sltiu (sltiu, not_74_out, not_75_out, OpCode[3], not_76_out, OpCode[1], OpCode[0]);
  assign bit_extender_15_out = {{3{1'b0}}, slti};  // Bit_Extender bit_extender_15
  Multiplier #(.width(4)) multiplier_13 (
    .a(bit_extender_15_out), .b(4'b1101), .out(multiplier_13_out));  // open: cin, cout
  assign cALU_JI = multiplier_1_out | multiplier_2_out | multiplier_4_out | multiplier_6_out | multiplier_8_out | multiplier_10_out | multiplier_13_out | multiplier_15_out | multiplier_17_out | multiplier_19_out | multiplier_21_out | multiplier_23_out | multiplier_25_out | multiplier_27_out | multiplier_30_out;  // OR_Gate or_10, 4 bits wide
  not not_77 (not_77_out, Func[0]);
  not not_78 (not_78_out, Func[4]);
  not not_79 (not_79_out, Func[1]);
  not not_80 (not_80_out, Func[2]);
  not not_81 (not_81_out, Func[3]);
  and u_add (add, Func[5], not_78_out, not_81_out, not_80_out, not_79_out, not_77_out);
  assign bit_extender_16_out = {{3{1'b0}}, divu};  // Bit_Extender bit_extender_16
  Multiplier #(.width(4)) multiplier_14 (
    .a(bit_extender_16_out), .b(4'b0100), .out(multiplier_14_out));  // open: cin, cout
  assign cALU_R = bit_extender_1_out | bit_extender_3_out | multiplier_3_out | multiplier_5_out | multiplier_7_out | multiplier_9_out | multiplier_11_out | multiplier_12_out | multiplier_14_out | multiplier_16_out | multiplier_18_out | multiplier_20_out | multiplier_22_out | multiplier_24_out | multiplier_26_out | multiplier_28_out | multiplier_29_out | multiplier_31_out | multiplier_32_out;  // OR_Gate or_11, 4 bits wide
  not not_82 (not_82_out, OpCode[5]);
  not not_83 (not_83_out, OpCode[4]);
  and u_andi (andi, not_82_out, not_83_out, OpCode[3], OpCode[2], not_91_out, not_89_out);
  assign bit_extender_17_out = {{3{1'b0}}, sltiu};  // Bit_Extender bit_extender_17
  Multiplier #(.width(4)) multiplier_15 (
    .a(bit_extender_17_out), .b(4'b1110), .out(multiplier_15_out));  // open: cin, cout
  not not_84 (not_84_out, Func[1]);
  not not_85 (not_85_out, Func[2]);
  not not_86 (not_86_out, Func[4]);
  not not_87 (not_87_out, Func[3]);
  and u_addu (addu, Func[5], not_86_out, not_87_out, not_85_out, not_84_out, Func[0]);
  assign bit_extender_18_out = {{3{1'b0}}, add};  // Bit_Extender bit_extender_18
  Multiplier #(.width(4)) multiplier_16 (
    .a(bit_extender_18_out), .b(4'b0101), .out(multiplier_16_out));  // open: cin, cout
  not not_88 (not_88_out, OpCode[5]);
  not not_89 (not_89_out, OpCode[0]);
  not not_90 (not_90_out, OpCode[4]);
  not not_91 (not_91_out, OpCode[1]);
  and u_ori (ori, not_88_out, not_90_out, OpCode[3], OpCode[2], not_96_out, OpCode[0]);
  assign bit_extender_19_out = {{3{1'b0}}, andi};  // Bit_Extender bit_extender_19
  Multiplier #(.width(4)) multiplier_17 (
    .a(bit_extender_19_out), .b(4'b1001), .out(multiplier_17_out));  // open: cin, cout
  not not_92 (not_92_out, Func[0]);
  not not_93 (not_93_out, Func[4]);
  not not_94 (not_94_out, Func[2]);
  not not_95 (not_95_out, Func[3]);
  and u_sub (sub, Func[5], not_93_out, not_95_out, not_94_out, Func[1], not_92_out);
  assign bit_extender_20_out = {{3{1'b0}}, addu};  // Bit_Extender bit_extender_20
  Multiplier #(.width(4)) multiplier_18 (
    .a(bit_extender_20_out), .b(4'b0110), .out(multiplier_18_out));  // open: cin, cout
  not not_96 (not_96_out, OpCode[1]);
  not not_97 (not_97_out, OpCode[4]);
  not not_98 (not_98_out, OpCode[5]);
  assign bit_extender_21_out = {{3{1'b0}}, ori};  // Bit_Extender bit_extender_21
  Multiplier #(.width(4)) multiplier_19 (
    .a(bit_extender_21_out), .b(4'b1010), .out(multiplier_19_out));  // open: cin, cout
  not not_99 (not_99_out, Func[2]);
  not not_100 (not_100_out, Func[4]);
  not not_101 (not_101_out, Func[3]);
  and u_subu (subu, Func[5], not_100_out, not_101_out, not_99_out, Func[1], Func[0]);
  assign bit_extender_22_out = {{3{1'b0}}, sub};  // Bit_Extender bit_extender_22
  Multiplier #(.width(4)) multiplier_20 (
    .a(bit_extender_22_out), .b(4'b0111), .out(multiplier_20_out));  // open: cin, cout
  not not_102 (not_102_out, OpCode[5]);
  not not_103 (not_103_out, OpCode[4]);
  not not_104 (not_104_out, OpCode[0]);
  and u_xori (xori, not_98_out, not_97_out, OpCode[3], OpCode[2], OpCode[1], not_104_out);
  assign bit_extender_23_out = {{3{1'b0}}, xori};  // Bit_Extender bit_extender_23
  Multiplier #(.width(4)) multiplier_21 (
    .a(bit_extender_23_out), .b(4'b1011), .out(multiplier_21_out));  // open: cin, cout
  not not_105 (not_105_out, Func[3]);
  not not_106 (not_106_out, Func[4]);
  not not_107 (not_107_out, Func[0]);
  not not_108 (not_108_out, Func[1]);
  and and_10 (\and , Func[5], not_106_out, not_105_out, Func[2], not_108_out, not_107_out);
  assign bit_extender_24_out = {{3{1'b0}}, subu};  // Bit_Extender bit_extender_24
  Multiplier #(.width(4)) multiplier_22 (
    .a(bit_extender_24_out), .b(4'b1000), .out(multiplier_22_out));  // open: cin, cout
  and lui (cIsLUI, not_102_out, not_103_out, OpCode[3], OpCode[2], OpCode[1], OpCode[0]);
  assign bit_extender_25_out = {{3{1'b0}}, cIsLUI};  // Bit_Extender bit_extender_25
  Multiplier #(.width(4)) multiplier_23 (
    .a(bit_extender_25_out), .b(4'b1111), .out(multiplier_23_out));  // open: cin, cout
  not not_109 (not_109_out, Func[4]);
  not not_110 (not_110_out, Func[3]);
  not not_111 (not_111_out, Func[1]);
  and or_12 (\or , Func[5], not_109_out, not_110_out, Func[2], not_111_out, Func[0]);
  assign bit_extender_26_out = {{3{1'b0}}, \and };  // Bit_Extender bit_extender_26
  Multiplier #(.width(4)) multiplier_24 (
    .a(bit_extender_26_out), .b(4'b1001), .out(multiplier_24_out));  // open: cin, cout
  not not_112 (not_112_out, OpCode[4]);
  not not_113 (not_113_out, OpCode[3]);
  not not_114 (not_114_out, OpCode[2]);
  and lw (cLW, OpCode[5], not_112_out, not_113_out, not_114_out, OpCode[1], OpCode[0]);
  assign bit_extender_27_out = {{3{1'b0}}, cLW};  // Bit_Extender bit_extender_27
  Multiplier #(.width(4)) multiplier_25 (
    .a(bit_extender_27_out), .b(4'b0110), .out(multiplier_25_out));  // open: cin, cout
  not not_115 (not_115_out, Func[3]);
  not not_116 (not_116_out, Func[4]);
  and u_nor (\nor , Func[5], not_116_out, not_115_out, Func[2], Func[1], Func[0]);
  assign bit_extender_28_out = {{3{1'b0}}, \or };  // Bit_Extender bit_extender_28
  Multiplier #(.width(4)) multiplier_26 (
    .a(bit_extender_28_out), .b(4'b1010), .out(multiplier_26_out));  // open: cin, cout
  not not_117 (not_117_out, OpCode[2]);
  not not_118 (not_118_out, OpCode[4]);
  and sw (cMemWrite, OpCode[5], not_118_out, OpCode[3], not_117_out, OpCode[1], OpCode[0]);
  assign bit_extender_29_out = {{3{1'b0}}, cMemWrite};  // Bit_Extender bit_extender_29
  Multiplier #(.width(4)) multiplier_27 (
    .a(bit_extender_29_out), .b(4'b0110), .out(multiplier_27_out));  // open: cin, cout
  not not_119 (not_119_out, Func[0]);
  not not_120 (not_120_out, Func[2]);
  not not_121 (not_121_out, Func[4]);
  not not_122 (not_122_out, Func[1]);
  and u_xor (\xor , Func[5], not_121_out, Func[3], not_120_out, not_122_out, not_119_out);
  assign bit_extender_30_out = {{3{1'b0}}, \nor };  // Bit_Extender bit_extender_30
  Multiplier #(.width(4)) multiplier_28 (
    .a(bit_extender_30_out), .b(4'b1100), .out(multiplier_28_out));  // open: cin, cout
  not not_123 (not_123_out, OpCode[5]);
  not not_124 (not_124_out, OpCode[3]);
  not not_125 (not_125_out, OpCode[4]);
  and u_beqinc (beqinc, not_123_out, not_125_out, not_124_out, OpCode[2], OpCode[1], not_129_out);
  not not_126 (not_126_out, Func[0]);
  not not_127 (not_127_out, Func[2]);
  not not_128 (not_128_out, Func[4]);
  and u_slt (slt, Func[5], not_128_out, Func[3], not_127_out, Func[1], not_126_out);
  assign bit_extender_31_out = {{3{1'b0}}, \xor };  // Bit_Extender bit_extender_31
  Multiplier #(.width(4)) multiplier_29 (
    .a(bit_extender_31_out), .b(4'b1011), .out(multiplier_29_out));  // open: cin, cout
  not not_129 (not_129_out, OpCode[0]);
  assign bit_extender_32_out = {{3{1'b0}}, beqinc};  // Bit_Extender bit_extender_32
  Multiplier #(.width(4)) multiplier_30 (
    .a(bit_extender_32_out), .b(4'b0101), .out(multiplier_30_out));  // open: cin, cout
  not not_130 (not_130_out, Func[2]);
  not not_131 (not_131_out, Func[4]);
  and u_sltu (sltu, Func[5], not_131_out, Func[3], not_130_out, Func[1], Func[0]);
  assign bit_extender_33_out = {{3{1'b0}}, slt};  // Bit_Extender bit_extender_33
  Multiplier #(.width(4)) multiplier_31 (
    .a(bit_extender_33_out), .b(4'b1101), .out(multiplier_31_out));  // open: cin, cout
  assign bit_extender_34_out = {{3{1'b0}}, sltu};  // Bit_Extender bit_extender_34
  Multiplier #(.width(4)) multiplier_32 (
    .a(bit_extender_34_out), .b(4'b1110), .out(multiplier_32_out));  // open: cin, cout
  or or_13 (or_13_out, sra, srl, sll);
  Multiplexer #(.width(4), .enable("false")) multiplexer_1 (.in0(cALU_JI), .in1(cALU_R), .out(cALU), .sel(OpZero));
  and and_11 (cShift, or_13_out, OpZero);
  and and_12 (and_12_out, jalr, OpZero);
  or or_14 (cFix_RA, and_12_out, jal);
  or or_15 (or_15_out, mult, divu);
  and and_13 (cIsMultDiv, or_15_out, OpZero);
  and and_14 (cIsMFLO, mflo, OpZero);
  and and_15 (cIsMFHI, mfhi, OpZero);
  and and_16 (cIsBEQINC, beqinc, not_132_out);
  not not_132 (not_132_out, Zero);
  or or_16 (cSXT, beq, bne, beqinc, addi, addiu, slti, sltiu, cLW, cMemWrite);
  or or_17 (or_17_out, jalr, jr);
  and and_17 (cJal_r, or_17_out, OpZero);

  // Other names for the same wires on the sheet: cRegW = cRegWrite; lui = cIsLUI; lw = cLW; sw = cMemWrite
endmodule
