// Logisim project regfile.circ as structural Verilog: 2 circuits, main circuit main
module main (
  input  [4:0] Read_Register_1,
  input  [4:0] Read_Register_2,
  input  [4:0] Write_Register,
  input  [31:0] Write_Data,
  input  Write_Enable,
  input  Clock,
  output [31:0] s0_Value,
  output [31:0] s1_Value,
  output [31:0] s2_Value,
  output [31:0] ra_Value,
  output [31:0] sp_Value,
  output [31:0] Read_Data_1,
  output [31:0] Read_Data_2
);

  registers registers_1 (
    .Clock(Clock), .Read_Register_1(Read_Register_1), .Read_Register_2(Read_Register_2),
    .Write_Register(Write_Register), .Write_Data(Write_Data), .Write_Enable(Write_Enable),
    .s0_Value(s0_Value), .s1_Value(s1_Value), .s2_Value(s2_Value), .ra_Value(ra_Value), .sp_Value(sp_Value),
    .Read_Data_1(Read_Data_1), .Read_Data_2(Read_Data_2));

  // Other names for the same wires on the sheet: clk = Clock; read_data1[31:0] = Read_Data_1;
  //   read_data2[31:0] = Read_Data_2; read_reg1[4:0] = Read_Register_1; read_reg2[4:0] = Read_Register_2;
  //   write_en = Write_Enable; write_reg[4:0] = Write_Register

  // Notes on the sheet:
  //   INPUTS to your circuit
  //   DON'T CHANGE THE LOCATIONS OF THE INPUTS AND OUTPUTS!
  //   These are DEBUG/TEST outputs from your circuit.
  //   OUTPUTS from your circuit
endmodule

// reg_files_sub
module registers (
  input  Clock,
  input  [4:0] Read_Register_1,
  input  [4:0] Read_Register_2,
  input  [4:0] Write_Register,
  input  [31:0] Write_Data,
  input  Write_Enable,
  output [31:0] s0_Value,
  output [31:0] s1_Value,
  output [31:0] s2_Value,
  output [31:0] ra_Value,
  output [31:0] sp_Value,
  output [31:0] Read_Data_1,
  output [31:0] Read_Data_2
);

  wire a0, a1, a2, a3, at, fp, gp, k0, k1, ra, s0, s1, s2, s3, s4, s5, s6, s7, sp, t0, t1, t2, t3, t4, t5,
       t6, t7, t8, t9, v0, v1;
  wire [31:0] a0r, a1r, a2r, a3r, atr, fpr, gpr, k0r, k1r, s3r, s4r, s5r, s6r, s7r, t0r, t1r, t2r, t3r, t4r,
       t5r, t6r, t7r, t8r, t9r, v0r, v1r, zeror;

  Demultiplexer #(.select(5), .disabled(0), .enable("false")) demultiplexer_1 (
    .out1(at), .out2(v0), .out3(v1), .out4(a0), .out5(a1), .out6(a2), .out7(a3), .out8(t0), .out9(t1),
    .out10(t2), .out11(t3), .out12(t4), .out13(t5), .out14(t6), .out15(t7), .out16(s0), .out17(s1),
    .out18(s2), .out19(s3), .out20(s4), .out21(s5), .out22(s6), .out23(s7), .out24(t8), .out25(t9),
    .out26(k0), .out27(k1), .out28(gp), .out29(sp), .out30(fp), .out31(ra), .in(Write_Enable),
    .sel(Write_Register));  // open: out0
  Register #(.width(32)) zero (.en(1'b0), .Q(zeror), .clr(1'b0));  // open: D, clk
  Register #(.width(32)) u_a1 (.D(Write_Data), .en(a1), .Q(a1r), .clk(Clock), .clr(1'b0));
  Register #(.width(32)) u_t2 (.D(Write_Data), .en(t2), .Q(t2r), .clk(Clock), .clr(1'b0));
  Register #(.width(32)) u_t7 (.D(Write_Data), .en(t7), .Q(t7r), .clk(Clock), .clr(1'b0));
  Register #(.width(32)) u_s4 (.D(Write_Data), .en(s4), .Q(s4r), .clk(Clock), .clr(1'b0));
  Register #(.width(32)) u_t8 (.D(Write_Data), .en(t8), .Q(t8r), .clk(Clock), .clr(1'b0));
  Register #(.width(32)) u_gp (.D(Write_Data), .en(gp), .Q(gpr), .clk(Clock), .clr(1'b0));
  Register #(.width(32)) u_at (.D(Write_Data), .en(at), .Q(atr), .clk(Clock), .clr(1'b0));
  Register #(.width(32)) u_a2 (.D(Write_Data), .en(a2), .Q(a2r), .clk(Clock), .clr(1'b0));
  Register #(.width(32)) u_t3 (.D(Write_Data), .en(t3), .Q(t3r), .clk(Clock), .clr(1'b0));
  Register #(.width(32)) u_s0 (.D(Write_Data), .en(s0), .Q(s0_Value), .clk(Clock), .clr(1'b0));
  Register #(.width(32)) u_s5 (.D(Write_Data), .en(s5), .Q(s5r), .clk(Clock), .clr(1'b0));
  Register #(.width(32)) u_t9 (.D(Write_Data), .en(t9), .Q(t9r), .clk(Clock), .clr(1'b0));
  Register #(.width(32)) u_sp (.D(Write_Data), .en(sp), .Q(sp_Value), .clk(Clock), .clr(1'b0));
  Register #(.width(32)) u_v0 (.D(Write_Data), .en(v0), .Q(v0r), .clk(Clock), .clr(1'b0));
  Register #(.width(32)) u_a3 (.D(Write_Data), .en(a3), .Q(a3r), .clk(Clock), .clr(1'b0));
  Register #(.width(32)) u_t4 (.D(Write_Data), .en(t4), .Q(t4r), .clk(Clock), .clr(1'b0));
  Register #(.width(32)) u_s1 (.D(Write_Data), .en(s1), .Q(s1_Value), .clk(Clock), .clr(1'b0));
  Register #(.width(32)) u_s6 (.D(Write_Data), .en(s6), .Q(s6r), .clk(Clock), .clr(1'b0));
  Register #(.width(32)) u_k0 (.D(Write_Data), .en(k0), .Q(k0r), .clk(Clock), .clr(1'b0));
  Register #(.width(32)) u_fp (.D(Write_Data), .en(fp), .Q(fpr), .clk(Clock), .clr(1'b0));
  Register #(.width(32)) u_v1 (.D(Write_Data), .en(v1), .Q(v1r), .clk(Clock), .clr(1'b0));
  Register #(.width(32)) u_t0 (.D(Write_Data), .en(t0), .Q(t0r), .clk(Clock), .clr(1'b0));
  Register #(.width(32)) u_t5 (.D(Write_Data), .en(t5), .Q(t5r), .clk(Clock), .clr(1'b0));
  Register #(.width(32)) u_s2 (.D(Write_Data), .en(s2), .Q(s2_Value), .clk(Clock), .clr(1'b0));
  Register #(.width(32)) u_s7 (.D(Write_Data), .en(s7), .Q(s7r), .clk(Clock), .clr(1'b0));
  Register #(.width(32)) u_k1 (.D(Write_Data), .en(k1), .Q(k1r), .clk(Clock), .clr(1'b0));
  Register #(.width(32)) u_ra (.D(Write_Data), .en(ra), .Q(ra_Value), .clk(Clock), .clr(1'b0));
  Register #(.width(32)) u_a0 (.D(Write_Data), .en(a0), .Q(a0r), .clk(Clock), .clr(1'b0));
  Register #(.width(32)) u_t1 (.D(Write_Data), .en(t1), .Q(t1r), .clk(Clock), .clr(1'b0));
  Register #(.width(32)) u_t6 (.D(Write_Data), .en(t6), .Q(t6r), .clk(Clock), .clr(1'b0));
  Register #(.width(32)) u_s3 (.D(Write_Data), .en(s3), .Q(s3r), .clk(Clock), .clr(1'b0));
  Multiplexer #(.select(5), .width(32), .enable("false")) multiplexer_1 (
    .in0(zeror), .in1(atr), .in2(v0r), .in3(v1r), .in4(a0r), .in5(a1r), .in6(a2r), .in7(a3r), .in8(t0r),
    .in9(t1r), .in10(t2r), .in11(t3r), .in12(t4r), .in13(t5r), .in14(t6r), .in15(t7r), .in16(s0_Value),
    .in17(s1_Value), .in18(s2_Value), .in19(s3r), .in20(s4r), .in21(s5r), .in22(s6r), .in23(s7r), .in24(t8r),
    .in25(t9r), .in26(k0r), .in27(k1r), .in28(gpr), .in29(sp_Value), .in30(fpr), .in31(ra_Value),
    .out(Read_Data_1), .sel(Read_Register_1));
  Multiplexer #(.select(5), .width(32), .enable("false")) multiplexer_2 (
    .in0(zeror), .in1(atr), .in2(v0r), .in3(v1r), .in4(a0r), .in5(a1r), .in6(a2r), .in7(a3r), .in8(t0r),
    .in9(t1r), .in10(t2r), .in11(t3r), .in12(t4r), .in13(t5r), .in14(t6r), .in15(t7r), .in16(s0_Value),
    .in17(s1_Value), .in18(s2_Value), .in19(s3r), .in20(s4r), .in21(s5r), .in22(s6r), .in23(s7r), .in24(t8r),
    .in25(t9r), .in26(k0r), .in27(k1r), .in28(gpr), .in29(sp_Value), .in30(fpr), .in31(ra_Value),
    .out(Read_Data_2), .sel(Read_Register_2));

  // Other names for the same wires on the sheet: rar[31:0] = ra_Value; read_data1[31:0] = Read_Data_1;
  //   read_data2[31:0] = Read_Data_2; read_reg1[4:0] = Read_Register_1; read_reg2[4:0] = Read_Register_2;
  //   s0r[31:0] = s0_Value; s1r[31:0] = s1_Value; s2r[31:0] = s2_Value; spr[31:0] = sp_Value; write_en = Write_Enable;
  //   write_reg[4:0] = Write_Register
endmodule
